# Fritzing sketch AutonomousBusdriver_steve (saved by Fritzing 0.9.3b)
breadboards: 1

parts:
  Raspberry_Pi_1 = Raspberry Pi 3 [part_number=RPI-3-V1.2]
  IC1 = L293D [package=THT]
  M1 = DC Motor
  M2 = DC Motor
  U1 = TRANSCHIPTC5747 [package=camera_sfv24r-2st_2]  # not connected

nets:
  N1: Raspberry_Pi_1.GPIO2, Raspberry_Pi_1.5V, IC1.Enable_1, IC1.+Vmotor, IC1.+V
  N2: Raspberry_Pi_1.GND, IC1.0V
  N3: Raspberry_Pi_1.GIPO17, IC1.In_3
  N4: Raspberry_Pi_1.GIPO27, IC1.In_4
  N5: Raspberry_Pi_1.GIPO22, IC1.Enable_2
  N6: Raspberry_Pi_1.GIPO19, IC1.In_2
  N7: Raspberry_Pi_1.GIPO26, IC1.In_1
  N8: IC1.Out_1_(_Controlled_by_Enable_1_), M1.pin_1
  N9: IC1.Out_2_(_Controlled_by_Enable_1_), M1.pin_2
  N10: IC1.Out_3_(_Controlled_by_Enable_2_), M2.pin_2
  N11: IC1.Out_4_(_Controlled_by_Enable_2_), M2.pin_1
